// Logisim project double_digit_tff.circ as structural Verilog: 1 circuit, main circuit main
module main (
  input  in_1,
  input  in_2,
  input  in_3,
  input  in_4
);

  wire and_1_out, and_2_out, and_3_out, and_4_out, clock_1_out, not_1_out, not_2_out, not_3_out, not_4_out,
       or_1_out, or_2_out, t_ff_1_q, t_ff_1_qn, t_ff_2_q, t_ff_2_qn, t_ff_3_q, t_ff_3_qn, t_ff_4_q,
       t_ff_4_qn, t_ff_5_q, t_ff_5_qn, t_ff_6_q, t_ff_6_qn, t_ff_7_q, t_ff_7_qn, t_ff_8_q;

  Clock clock_1 (.out(clock_1_out));
  and and_1 (and_1_out, clock_1_out, in_1);
  or or_1 (or_1_out, in_3, or_2_out, and_3_out);
  and and_2 (and_2_out, in_1, t_ff_4_qn);
  or or_2 (or_2_out, in_3, and_4_out);
  T_Flip_Flop t_ff_1 (.clk(and_1_out), .T(in_2), .Q(t_ff_1_q), .Qn(t_ff_1_qn), .reset(or_1_out));  // open: preset, en
  T_Flip_Flop t_ff_2 (.clk(t_ff_1_qn), .T(in_2), .Q(t_ff_2_q), .Qn(t_ff_2_qn), .reset(or_1_out));  // open: preset, en
  T_Flip_Flop t_ff_3 (.clk(t_ff_2_qn), .T(in_2), .Q(t_ff_3_q), .Qn(t_ff_3_qn), .reset(or_1_out));  // open: preset, en
  T_Flip_Flop t_ff_4 (.clk(t_ff_3_qn), .T(in_2), .Q(t_ff_4_q), .Qn(t_ff_4_qn), .reset(or_1_out));  // open: preset, en
  T_Flip_Flop t_ff_5 (.clk(and_2_out), .T(in_4), .Q(t_ff_5_q), .Qn(t_ff_5_qn), .reset(or_2_out));  // open: preset, en
  T_Flip_Flop t_ff_6 (.clk(t_ff_5_qn), .T(in_4), .Q(t_ff_6_q), .Qn(t_ff_6_qn), .reset(or_2_out));  // open: preset, en
  T_Flip_Flop t_ff_7 (.clk(t_ff_6_qn), .T(in_4), .Q(t_ff_7_q), .Qn(t_ff_7_qn), .reset(or_2_out));  // open: preset, en
  T_Flip_Flop t_ff_8 (.clk(t_ff_7_qn), .T(in_4), .Q(t_ff_8_q), .reset(or_2_out));  // open: Qn, preset, en
  not not_1 (not_1_out, t_ff_1_q);
  not not_2 (not_2_out, t_ff_3_q);
  not not_3 (not_3_out, t_ff_5_q);
  not not_4 (not_4_out, t_ff_8_q);
  LED led_1 (.in(t_ff_4_q));
  and and_3 (and_3_out, not_1_out, t_ff_2_q, not_2_out, t_ff_4_q);
  LED led_2 (.in(t_ff_8_q));
  and and_4 (and_4_out, not_3_out, t_ff_6_q, t_ff_7_q, not_4_out);
  LED led_3 (.in(t_ff_1_q));
  LED led_4 (.in(t_ff_2_q));
  LED led_5 (.in(t_ff_3_q));
  LED led_6 (.in(t_ff_5_q));
  LED led_7 (.in(t_ff_6_q));
  LED led_8 (.in(t_ff_7_q));
endmodule
